# Fritzing sketch Board for project PCB (saved by Fritzing 0.9.3b)
circuit board: 6.70177cm x 3.85cm
circuit board: 5.2cm x 3.2cm
breadboards: 1

parts:
  UP = Pushbutton [part_number=COM-09190 package="[THT]"]
  HOME = Pushbutton [part_number=COM-09190 package="[THT]"]
  R9 = Resistor [tolerance=±5% resistance=10k package=THT]
  R10 = Resistor [tolerance=±5% resistance=10k package=THT]
  DOWN = Pushbutton [part_number=COM-09190 package="[THT]"]
  SELECT = Pushbutton [part_number=COM-09190 package="[THT]"]
  U_S_D_H_G = Resistor [tolerance=±5% resistance=10k package=THT]
  WGH_SENSOR = HX711 Weighing Sensor Module
  ARDUINO = female pin header, 12 pins [form="♀ (female)"]
  ARDUINO_2 = female pin header, 12 pins [form="♀ (female)"]
  SCREEN_HEADER = female pin header, 11 pins [form="♀ (female)"]
  part = Resistor [tolerance=±5% resistance=10k package=THT]
  5v = female pin header, 6 pins [form="♀ (female)"]
  U_S_D_H_G_5v = female pin header, 6 pins [form="♀ (female)"]

nets:
  N1: UP.Pin_1, HOME.Pin_1, HOME.Pin_2, DOWN.Pin_1, DOWN.Pin_2, SELECT.Pin_1, SELECT.Pin_2, 5v.pin6
  N2: UP.Pin_3, R9.Pin_1, 5v.pin1
  N3: HOME.Pin_3, U_S_D_H_G.Pin_1, 5v.pin4
  N4: R9.Pin_0, R10.Pin_0, U_S_D_H_G.Pin_0, part.Pin_0, 5v.pin5
  N5: R10.Pin_1, SELECT.Pin_3, 5v.pin2
  N6: DOWN.Pin_3, DOWN.Pin_4, part.Pin_1, 5v.pin3
  N7: WGH_SENSOR.VCC, ARDUINO.pin1, SCREEN_HEADER.pin1, U_S_D_H_G_5v.pin6
  N8: WGH_SENSOR.GND, ARDUINO.pin2, SCREEN_HEADER.pin3, U_S_D_H_G_5v.pin5
  N9: WGH_SENSOR.DO/RX, ARDUINO.pin7
  N10: WGH_SENSOR.CK/TX, ARDUINO.pin8
  N11: ARDUINO.pin9, SCREEN_HEADER.pin4
  N12: ARDUINO.pin11, SCREEN_HEADER.pin6
  N13: ARDUINO.pin12, SCREEN_HEADER.pin7
  N14: ARDUINO_2.pin7, U_S_D_H_G_5v.pin1
  N15: ARDUINO_2.pin8, U_S_D_H_G_5v.pin2
  N16: ARDUINO_2.pin9, U_S_D_H_G_5v.pin3
  N17: ARDUINO_2.pin10, U_S_D_H_G_5v.pin4
  N18: ARDUINO_2.pin11, SCREEN_HEADER.pin9
  N19: ARDUINO_2.pin12, SCREEN_HEADER.pin8

custom parts:
  Pushbutton: A generic pushbutton. This is a standard 12mm square momentary button. What we really like is the large button head and good tactile feel (it ‘clicks’ really well). This button is great for user input on a PCB or a good, big reset button on a breadboard. Breadboard friendly! SparkFun Storefront SKU: COM-09190 Modified by: Ho Yun "Bobby" Chan @ SparkFun Electronics Inc.
